# Fritzing sketch connector-pcb (saved by Fritzing 0.9.2b)
circuit board: 5.3cm x 1.4cm
breadboards: 1

parts:
  BME280 = male pin header, 7 pins [form="♂ (male)"]
  TSL25911 = male pin header, 7 pins [form="♂ (male)"]
  R1 = Resistor [tolerance=±5% resistance=220 package=THT]
  LED = LED - 5mm [color="Red (633nm)" package="5 mm [THT]"]
  Raspberry_Pi1 = Raspberry Pi 2

nets:
  N1: BME280.pin1, TSL25911.pin1, R1.Pin_0, Raspberry_Pi1.GND
  3V3: BME280.pin3, TSL25911.pin3, Raspberry_Pi1.3v3, Raspberry_Pi1.3V3
  N2: BME280.pin4, TSL25911.pin4, Raspberry_Pi1.GPIO3
  N3: BME280.pin5, TSL25911.pin5, Raspberry_Pi1.GPIO2
  N4: R1.Pin_1, LED.cathode
  N5: LED.anode, Raspberry_Pi1.GPIO26

notes:
  GND
  3.3V
  GPIO26
